// Logisim project built_cpu.circ as structural Verilog: 23 circuits, main circuit RAM4BIT
module main (
  input  in_1,
  input  in_2
);

  wire address_reg_1_a0out, address_reg_1_a1out, address_reg_1_a2out, alu_1_negative, alu_1_overflow,
       alu_1_zero, AOUT0, AOUT1, AOUT2, AOUT3, binary_to_decimal_1_a0, binary_to_decimal_1_a1,
       binary_to_decimal_1_b0, binary_to_decimal_1_b1, binary_to_decimal_1_b2, binary_to_decimal_1_b3,
       binary_to_decimal_1_b4, binary_to_decimal_1_b5, binary_to_decimal_1_b6, binary_to_decimal_1_b7,
       binary_to_decimal_1_b8, binary_to_decimal_1_b9, CLCK, controlunit_1_a0, D0_BUS, D0_RAM, D1_BUS,
       D1_RAM, D2_BUS, D2_RAM, D3_BUS, D3_RAM, d_register_1_d0out, d_register_1_d1out, d_register_1_d2out,
       d_register_1_d3out, ENABLE_LEFT, ENABLE_R0, ENABLE_R1, ENABLE_RAM, ENABLE_RIGHT, HALT, INCR_PC,
       ir_1_d0out, ir_1_d1out, ir_1_d2out, ir_1_d3out, left_reg_1_d0_out, left_reg_1_d1_out,
       left_reg_1_d2_out, left_reg_1_d3_out, mar_1_a0out, mar_1_a1out, mar_1_a2out, mbr_1_d0out, mbr_1_d1out,
       mbr_1_d2out, mbr_1_d3out, nums_1_fifth, nums_1_first, nums_1_fourth, nums_1_second, nums_1_seventh,
       nums_1_sixth, nums_1_third, or_5_out, or_6_out, or_7_out, or_8_out, pc_1_a0, pc_1_a1, pc_1_a2, R0OUT0,
       R0OUT1, R0OUT2, R0OUT3, R1OUT0, R1OUT1, R1OUT2, R1OUT3, RAM0_0BUS, RAM0_1BUS, RAM0_2BUS, RAM0_3BUS,
       ram4bit_1_d1out, ram4bit_1_d2out, ram4bit_1_d3out, ram4bit_1_d4out, READ_AR, READ_LEFT, READ_PC,
       READ_RIGHT, right_reg_1_d0_out, right_reg_1_d1_out, right_reg_1_d2_out, right_reg_1_d3_out, SUB_ALU,
       WRITE_AR, WRITE_IR, WRITE_MAR, WRITE_MBR, WRITE_R0, WRITE_R1, WRITE_RAM;

  or or_1 (D3_BUS, R0OUT3, R1OUT3, AOUT3, D3_RAM);
  or or_2 (D2_BUS, R0OUT2, R1OUT2, AOUT2, D2_RAM);
  or or_3 (D1_BUS, D1_RAM, R0OUT1, AOUT1, R1OUT1);
  or or_4 (D0_BUS, D0_RAM, R0OUT0, R1OUT0, AOUT0);
  MBR mbr_1 (
    .CLCK(CLCK), .WRITE_MBR(WRITE_MBR), .D0(D0_RAM), .D1(D1_RAM), .D2(D2_RAM), .D3(D3_RAM),
    .D0OUT(mbr_1_d0out), .D1OUT(mbr_1_d1out), .D2OUT(mbr_1_d2out), .D3OUT(mbr_1_d3out));
  and and_1 (CLCK, ~HALT, in_1);  // AND_Gate
  RAM4BIT ram4bit_1 (
    .CLK(CLCK), .A3(mar_1_a2out), .A2(mar_1_a1out), .A1(mar_1_a0out), .Mode(WRITE_RAM), .D4in(D3_BUS),
    .D3in(D2_BUS), .D2in(D1_BUS), .D1in(D0_BUS), .D4out(ram4bit_1_d4out), .D3out(ram4bit_1_d3out),
    .D2out(ram4bit_1_d2out), .D1out(ram4bit_1_d1out), .RAM0_3(RAM0_3BUS), .RAM0_2(RAM0_2BUS),
    .RAM0_1(RAM0_1BUS), .RAM0_0(RAM0_0BUS));
  MAR mar_1 (
    .CLCK(CLCK), .WRITE_MAR(WRITE_MAR), .A2(or_5_out), .A1(or_6_out), .A0(or_7_out), .A0OUT(mar_1_a0out),
    .A1OUT(mar_1_a1out), .A2OUT(mar_1_a2out));
  and and_2 (D3_RAM, ENABLE_RAM, ram4bit_1_d4out);
  and and_3 (D2_RAM, ENABLE_RAM, ram4bit_1_d3out);
  and and_4 (D1_RAM, ENABLE_RAM, ram4bit_1_d2out);
  and and_5 (D0_RAM, ENABLE_RAM, ram4bit_1_d1out);
  or or_5 (or_5_out, address_reg_1_a2out, pc_1_a2);
  or or_6 (or_6_out, address_reg_1_a1out, pc_1_a1);
  or or_7 (or_7_out, address_reg_1_a0out, pc_1_a0);
  PC pc_1 (.RESET(in_2), .CLCK(CLCK), .ADD_TO_PC(INCR_PC), .READ_PC(READ_PC), .A2(pc_1_a2), .A1(pc_1_a1), .A0(pc_1_a0));
  IR ir_1 (
    .CLCK(CLCK), .WRITE_IR(WRITE_IR), .D0(mbr_1_d0out), .D1(mbr_1_d1out), .D2(mbr_1_d2out), .D3(mbr_1_d3out),
    .D0OUT(ir_1_d0out), .D1OUT(ir_1_d1out), .D2OUT(ir_1_d2out), .D3OUT(ir_1_d3out));
  LEFT_REG left_reg_1 (
    .ENABLE_LEFT(ENABLE_LEFT), .CLCK(CLCK), .READ_LEFT(READ_LEFT), .D3(D3_BUS), .D2(D2_BUS), .D1(D1_BUS),
    .D0(D0_BUS), .D3_OUT(left_reg_1_d3_out), .D2_OUT(left_reg_1_d2_out), .D1_OUT(left_reg_1_d1_out),
    .D0_OUT(left_reg_1_d0_out));
  RIGHT_REG right_reg_1 (
    .ENABLE_RIGHT(ENABLE_RIGHT), .CLCK(CLCK), .READ_RIGHT(READ_RIGHT), .D3(D3_BUS), .D2(D2_BUS), .D1(D1_BUS),
    .D0(D0_BUS), .D3_OUT(right_reg_1_d3_out), .D2_OUT(right_reg_1_d2_out), .D1_OUT(right_reg_1_d1_out),
    .D0_OUT(right_reg_1_d0_out));
  D_REGISTER d_register_1 (
    .D3(RAM0_3BUS), .D2(RAM0_2BUS), .D1(RAM0_1BUS), .D0(RAM0_0BUS), .CLCK(CLCK), .D3OUT(d_register_1_d3out),
    .D2OUT(d_register_1_d2out), .D1OUT(d_register_1_d1out), .D0OUT(d_register_1_d0out));
  ADDRESS_REG address_reg_1 (
    .READ_ADDRREG(READ_AR), .CLCK(CLCK), .WRITE_ADDREG(WRITE_AR), .A0(controlunit_1_a0),
    .A2OUT(address_reg_1_a2out), .A1OUT(address_reg_1_a1out), .A0OUT(address_reg_1_a0out));  // open: A1, A2
  R0 r0_1 (
    .D3(D3_BUS), .D2(D2_BUS), .D1(D1_BUS), .D0(D0_BUS), .WRITE_R0(WRITE_R0), .CLCK(CLCK), .ENABLE(ENABLE_R0),
    .D3OUT(R0OUT3), .D2OUT(R0OUT2), .D1OUT(R0OUT1), .D0OUT(R0OUT0));
  ControlUnit controlunit_1 (
    .RESET(in_2), .CLCK(CLCK), .IN1(ir_1_d0out), .IN2(ir_1_d1out), .IN3(ir_1_d2out), .IN4(ir_1_d3out),
    .INCR_PC(INCR_PC), .WRITE_MBR(WRITE_MBR), .WRITE_IR(WRITE_IR), .A0(controlunit_1_a0),
    .WRITE_R0(WRITE_R0), .WRITE_R1(WRITE_R1), .ENABLE_R0(ENABLE_R0), .ENABLE_R1(ENABLE_R1),
    .ENABLE_RAM(ENABLE_RAM), .WRITE_RAM(WRITE_RAM), .WRITE_MAR(WRITE_MAR), .MODE_ALU(SUB_ALU),
    .ENABLE_LEFT(ENABLE_LEFT), .ENABLE_RIGHT(ENABLE_RIGHT), .READ_PC(READ_PC), .READ_LEFT(READ_LEFT),
    .READ_RIGHT(READ_RIGHT), .WRITE_AR(WRITE_AR), .READ_AR(READ_AR), .HALT(HALT));
  ALU alu_1 (
    .L3(left_reg_1_d3_out), .L2(left_reg_1_d2_out), .L1(left_reg_1_d1_out), .L0(left_reg_1_d0_out),
    .R3(right_reg_1_d3_out), .R2(right_reg_1_d2_out), .R1(right_reg_1_d1_out), .R0(right_reg_1_d0_out),
    .CLCK(CLCK), .SUB(SUB_ALU), .Zero(alu_1_zero), .Negative(alu_1_negative), .Overflow(alu_1_overflow),
    .AOUT3(AOUT3), .AOUT2(AOUT2), .AOUT1(AOUT1), .AOUT0(AOUT0));
  BINARY_TO_DECIMAL binary_to_decimal_1 (
    .D3(d_register_1_d3out), .D2(d_register_1_d2out), .D1(d_register_1_d1out), .D0(d_register_1_d0out),
    .A0(binary_to_decimal_1_a0), .A1(binary_to_decimal_1_a1), .B0(binary_to_decimal_1_b0),
    .B1(binary_to_decimal_1_b1), .B2(binary_to_decimal_1_b2), .B3(binary_to_decimal_1_b3),
    .B4(binary_to_decimal_1_b4), .B5(binary_to_decimal_1_b5), .B6(binary_to_decimal_1_b6),
    .B7(binary_to_decimal_1_b7), .B8(binary_to_decimal_1_b8), .B9(binary_to_decimal_1_b9));
  or or_8 (or_8_out, binary_to_decimal_1_a0, binary_to_decimal_1_a1);
  R1 r1_1 (
    .D3(D3_BUS), .D2(D2_BUS), .D1(D1_BUS), .D0(D0_BUS), .WRITE_R1(WRITE_R1), .CLCK(CLCK), .ENABLE(ENABLE_R1),
    .D3OUT(R1OUT3), .D2OUT(R1OUT2), .D1OUT(R1OUT1), .D0OUT(R1OUT0));
  StatusReg statusreg_1 (.ZERO(alu_1_zero), .NEGATIVE(alu_1_negative), .OVERFLOW(alu_1_overflow), .CLCK(CLCK));
  NUMS nums_1 (
    .Z_ERO(binary_to_decimal_1_b0), .O_NE(binary_to_decimal_1_b1), .TWO(binary_to_decimal_1_b2),
    .THREE(binary_to_decimal_1_b3), .FOUR(binary_to_decimal_1_b4), .FIVE(binary_to_decimal_1_b5),
    .SIX(binary_to_decimal_1_b6), .SEVEN(binary_to_decimal_1_b7), .EIGHT(binary_to_decimal_1_b8),
    .NINE(binary_to_decimal_1_b9), .FIRST(nums_1_first), .SECOND(nums_1_second), .THIRD(nums_1_third),
    .FOURTH(nums_1_fourth), .FIFTH(nums_1_fifth), .SIXTH(nums_1_sixth), .SEVENTH(nums_1_seventh));
  _7_Segment_Display #(.decimalPoint("false")) u_7_segment_display_1 (
    .f(or_8_out), .a(binary_to_decimal_1_a0), .b(binary_to_decimal_1_a0), .e(or_8_out),
    .d(binary_to_decimal_1_a0), .c(binary_to_decimal_1_a0));  // open: g
  _7_Segment_Display #(.decimalPoint("false")) u_7_segment_display_2 (
    .g(nums_1_first), .f(nums_1_second), .a(nums_1_third), .b(nums_1_fourth), .e(nums_1_seventh),
    .d(nums_1_sixth), .c(nums_1_fifth));

  // Other names for the same wires on the sheet: RESET = in_2

  // Notes on the sheet:
  //   Increment PC to 0010 by clicking reset twice(on and off)
  //   then begin clock
endmodule

module RAM4BIT (
  input  CLK,
  input  A3,
  input  A2,
  input  A1,
  input  Mode,
  input  D4in,
  input  D3in,
  input  D2in,
  input  D1in,
  output D4out,
  output D3out,
  output D2out,
  output D1out,
  output RAM0_3,
  output RAM0_2,
  output RAM0_1,
  output RAM0_0
);

  wire and_1_out, and_2_out, and_3_out, and_4_out, and_5_out, and_6_out, and_7_out, and_8_out, and_9_out,
       and_10_out, and_11_out, and_12_out, and_13_out, and_14_out, and_15_out, and_16_out, and_17_out,
       and_18_out, and_19_out, and_20_out, and_21_out, and_22_out, and_23_out, and_24_out, and_25_out,
       and_26_out, and_27_out, and_28_out, and_29_out, and_30_out, and_31_out, and_32_out, and_33_out,
       and_34_out, and_35_out, and_36_out, and_37_out, and_38_out, and_39_out, and_40_out, and_41_out,
       and_42_out, and_43_out, and_44_out, and_45_out, and_46_out, and_47_out, and_48_out, and_49_out,
       and_50_out, and_51_out, and_52_out, and_53_out, and_54_out, and_55_out, and_56_out, and_57_out,
       and_58_out, and_59_out, and_60_out, and_61_out, and_62_out, and_63_out, and_64_out, and_65_out,
       and_66_out, and_67_out, and_68_out, and_69_out, and_70_out, and_71_out, and_72_out, and_73_out,
       and_74_out, and_75_out, and_76_out, and_77_out, and_78_out, and_79_out, and_80_out, d_ff_1_q,
       d_ff_2_q, d_ff_3_q, d_ff_4_q, d_ff_5_q, d_ff_6_q, d_ff_7_q, d_ff_9_q, d_ff_10_q, d_ff_11_q, d_ff_12_q,
       d_ff_13_q, d_ff_14_q, d_ff_15_q, d_ff_17_q, d_ff_18_q, d_ff_19_q, d_ff_20_q, d_ff_21_q, d_ff_22_q,
       d_ff_23_q, d_ff_25_q, d_ff_26_q, d_ff_27_q, d_ff_28_q, d_ff_29_q, d_ff_30_q, d_ff_31_q, not_1_out,
       not_2_out, not_3_out, not_4_out, not_5_out, not_6_out, not_7_out, not_8_out, not_9_out, not_10_out,
       not_11_out, not_12_out, not_13_out;

  not not_1 (not_1_out, A1);
  not not_2 (not_2_out, A2);
  not not_3 (not_3_out, A2);
  not not_4 (not_4_out, A1);
  not not_5 (not_5_out, A3);
  not not_6 (not_6_out, A3);
  not not_7 (not_7_out, A1);
  not not_8 (not_8_out, A3);
  not not_9 (not_9_out, A2);
  not not_10 (not_10_out, A3);
  not not_11 (not_11_out, A2);
  not not_12 (not_12_out, A1);
  and and_1 (and_1_out, A3, A2, CLK, A1);
  and and_2 (and_2_out, and_1_out, Mode);
  and and_3 (and_3_out, A3, A2, CLK, not_1_out);
  and and_4 (and_4_out, and_3_out, Mode);
  and and_5 (and_5_out, A3, not_2_out, CLK, A1);
  and and_6 (and_6_out, and_5_out, Mode);
  and and_7 (and_7_out, A3, not_3_out, CLK, not_4_out);
  and and_8 (and_8_out, and_7_out, Mode);
  and and_9 (and_9_out, not_5_out, A2, CLK, A1);
  and and_10 (and_10_out, and_9_out, Mode);
  and and_11 (and_11_out, not_6_out, A2, CLK, not_7_out);
  and and_12 (and_12_out, and_11_out, Mode);
  and and_13 (and_13_out, not_8_out, not_9_out, CLK, A1);
  and and_14 (and_14_out, and_13_out, Mode);
  and and_15 (and_15_out, not_10_out, CLK, not_11_out, not_12_out);
  and and_16 (and_16_out, and_15_out, Mode);
  and and_17 (and_17_out, and_1_out, Mode, D4in);
  D_Flip_Flop #(.trigger("high")) d_ff_1 (.D(and_17_out), .clk(and_2_out), .Q(d_ff_1_q));  // open: Qn, preset, reset
  and and_18 (and_18_out, and_3_out, Mode, D4in);
  D_Flip_Flop #(.trigger("high")) d_ff_2 (.D(and_18_out), .clk(and_4_out), .Q(d_ff_2_q));  // open: Qn, preset, reset
  and and_19 (and_19_out, and_5_out, Mode, D4in);
  D_Flip_Flop #(.trigger("high")) d_ff_3 (.D(and_19_out), .clk(and_6_out), .Q(d_ff_3_q));  // open: Qn, preset, reset
  and and_20 (and_20_out, and_7_out, Mode, D4in);
  D_Flip_Flop #(.trigger("high")) d_ff_4 (.D(and_20_out), .clk(and_8_out), .Q(d_ff_4_q));  // open: Qn, preset, reset
  and and_21 (and_21_out, and_9_out, Mode, D4in);
  D_Flip_Flop #(.trigger("high")) d_ff_5 (.D(and_21_out), .clk(and_10_out), .Q(d_ff_5_q));  // open: Qn, preset, reset
  and and_22 (and_22_out, and_11_out, Mode, D4in);
  D_Flip_Flop #(.trigger("high")) d_ff_6 (.D(and_22_out), .clk(and_12_out), .Q(d_ff_6_q));  // open: Qn, preset, reset
  and and_23 (and_23_out, and_13_out, Mode, D4in);
  D_Flip_Flop #(.trigger("high")) d_ff_7 (.D(and_23_out), .clk(and_14_out), .Q(d_ff_7_q));  // open: Qn, preset, reset
  and and_24 (and_24_out, and_15_out, Mode, D4in);
  D_Flip_Flop #(.trigger("high")) d_ff_8 (.D(and_24_out), .clk(and_16_out), .Q(RAM0_3));  // open: Qn, preset, reset
  not not_13 (not_13_out, Mode);
  or or_1 (D4out, and_25_out, and_26_out, and_27_out, and_28_out, and_29_out, and_30_out, and_31_out, and_32_out);
  and and_25 (and_25_out, d_ff_1_q, and_1_out, not_13_out);
  and and_26 (and_26_out, d_ff_2_q, and_3_out, not_13_out);
  and and_27 (and_27_out, d_ff_3_q, and_5_out, not_13_out);
  and and_28 (and_28_out, d_ff_4_q, and_7_out, not_13_out);
  and and_29 (and_29_out, d_ff_5_q, and_9_out, not_13_out);
  and and_30 (and_30_out, d_ff_6_q, and_11_out, not_13_out);
  and and_31 (and_31_out, d_ff_7_q, and_13_out, not_13_out);
  and and_32 (and_32_out, RAM0_3, and_15_out, not_13_out);
  and and_33 (and_33_out, and_1_out, Mode, D3in);
  D_Flip_Flop #(.trigger("high")) d_ff_9 (.D(and_33_out), .clk(and_2_out), .Q(d_ff_9_q));  // open: Qn, preset, reset
  and and_34 (and_34_out, and_3_out, Mode, D3in);
  D_Flip_Flop #(.trigger("high")) d_ff_10 (.D(and_34_out), .clk(and_4_out), .Q(d_ff_10_q));  // open: Qn, preset, reset
  and and_35 (and_35_out, and_5_out, Mode, D3in);
  D_Flip_Flop #(.trigger("high")) d_ff_11 (.D(and_35_out), .clk(and_6_out), .Q(d_ff_11_q));  // open: Qn, preset, reset
  and and_36 (and_36_out, and_7_out, Mode, D3in);
  D_Flip_Flop #(.trigger("high")) d_ff_12 (.D(and_36_out), .clk(and_8_out), .Q(d_ff_12_q));  // open: Qn, preset, reset
  and and_37 (and_37_out, and_9_out, Mode, D3in);
  D_Flip_Flop #(.trigger("high")) d_ff_13 (.D(and_37_out), .clk(and_10_out), .Q(d_ff_13_q));  // open: Qn, preset, reset
  and and_38 (and_38_out, and_11_out, Mode, D3in);
  D_Flip_Flop #(.trigger("high")) d_ff_14 (.D(and_38_out), .clk(and_12_out), .Q(d_ff_14_q));  // open: Qn, preset, reset
  and and_39 (and_39_out, and_13_out, Mode, D3in);
  D_Flip_Flop #(.trigger("high")) d_ff_15 (.D(and_39_out), .clk(and_14_out), .Q(d_ff_15_q));  // open: Qn, preset, reset
  and and_40 (and_40_out, and_15_out, Mode, D3in);
  D_Flip_Flop #(.trigger("high")) d_ff_16 (.D(and_40_out), .clk(and_16_out), .Q(RAM0_2));  // open: Qn, preset, reset
  or or_2 (D3out, and_41_out, and_42_out, and_43_out, and_44_out, and_45_out, and_46_out, and_47_out, and_48_out);
  and and_41 (and_41_out, d_ff_9_q, and_1_out, not_13_out);
  and and_42 (and_42_out, d_ff_10_q, and_3_out, not_13_out);
  and and_43 (and_43_out, d_ff_11_q, and_5_out, not_13_out);
  and and_44 (and_44_out, d_ff_12_q, and_7_out, not_13_out);
  and and_45 (and_45_out, d_ff_13_q, and_9_out, not_13_out);
  and and_46 (and_46_out, d_ff_14_q, and_11_out, not_13_out);
  and and_47 (and_47_out, d_ff_15_q, and_13_out, not_13_out);
  and and_48 (and_48_out, RAM0_2, and_15_out, not_13_out);
  Clock clock_1 ();  // open: out
  and and_49 (and_49_out, and_1_out, Mode, D2in);
  and and_50 (and_50_out, and_3_out, Mode, D2in);
  and and_51 (and_51_out, and_5_out, Mode, D2in);
  and and_52 (and_52_out, and_7_out, Mode, D2in);
  and and_53 (and_53_out, and_9_out, Mode, D2in);
  and and_54 (and_54_out, and_11_out, Mode, D2in);
  and and_55 (and_55_out, and_13_out, Mode, D2in);
  and and_56 (and_56_out, and_15_out, Mode, D2in);
  D_Flip_Flop #(.trigger("high")) d_ff_17 (.D(and_49_out), .clk(and_2_out), .Q(d_ff_17_q));  // open: Qn, preset, reset
  D_Flip_Flop #(.trigger("high")) d_ff_18 (.D(and_50_out), .clk(and_4_out), .Q(d_ff_18_q));  // open: Qn, preset, reset
  D_Flip_Flop #(.trigger("high")) d_ff_19 (.D(and_51_out), .clk(and_6_out), .Q(d_ff_19_q));  // open: Qn, preset, reset
  D_Flip_Flop #(.trigger("high")) d_ff_20 (.D(and_52_out), .clk(and_8_out), .Q(d_ff_20_q));  // open: Qn, preset, reset
  D_Flip_Flop #(.trigger("high")) d_ff_21 (.D(and_53_out), .clk(and_10_out), .Q(d_ff_21_q));  // open: Qn, preset, reset
  D_Flip_Flop #(.trigger("high")) d_ff_22 (.D(and_54_out), .clk(and_12_out), .Q(d_ff_22_q));  // open: Qn, preset, reset
  D_Flip_Flop #(.trigger("high")) d_ff_23 (.D(and_55_out), .clk(and_14_out), .Q(d_ff_23_q));  // open: Qn, preset, reset
  D_Flip_Flop #(.trigger("high")) d_ff_24 (.D(and_56_out), .clk(and_16_out), .Q(RAM0_1));  // open: Qn, preset, reset
  or or_3 (D2out, and_57_out, and_58_out, and_59_out, and_60_out, and_61_out, and_62_out, and_63_out, and_64_out);
  and and_57 (and_57_out, d_ff_17_q, and_1_out, not_13_out);
  and and_58 (and_58_out, d_ff_18_q, and_3_out, not_13_out);
  and and_59 (and_59_out, d_ff_19_q, and_5_out, not_13_out);
  and and_60 (and_60_out, d_ff_20_q, and_7_out, not_13_out);
  and and_61 (and_61_out, d_ff_21_q, and_9_out, not_13_out);
  and and_62 (and_62_out, d_ff_22_q, and_11_out, not_13_out);
  and and_63 (and_63_out, d_ff_23_q, and_13_out, not_13_out);
  and and_64 (and_64_out, RAM0_1, and_15_out, not_13_out);
  and and_65 (and_65_out, and_1_out, Mode, D1in);
  D_Flip_Flop #(.trigger("high")) d_ff_25 (.D(and_65_out), .clk(and_2_out), .Q(d_ff_25_q));  // open: Qn, preset, reset
  and and_66 (and_66_out, and_3_out, Mode, D1in);
  D_Flip_Flop #(.trigger("high")) d_ff_26 (.D(and_66_out), .clk(and_4_out), .Q(d_ff_26_q));  // open: Qn, preset, reset
  and and_67 (and_67_out, and_5_out, Mode, D1in);
  D_Flip_Flop #(.trigger("high")) d_ff_27 (.D(and_67_out), .clk(and_6_out), .Q(d_ff_27_q));  // open: Qn, preset, reset
  and and_68 (and_68_out, and_7_out, Mode, D1in);
  D_Flip_Flop #(.trigger("high")) d_ff_28 (.D(and_68_out), .clk(and_8_out), .Q(d_ff_28_q));  // open: Qn, preset, reset
  and and_69 (and_69_out, and_9_out, Mode, D1in);
  D_Flip_Flop #(.trigger("high")) d_ff_29 (.D(and_69_out), .clk(and_10_out), .Q(d_ff_29_q));  // open: Qn, preset, reset
  and and_70 (and_70_out, and_11_out, Mode, D1in);
  D_Flip_Flop #(.trigger("high")) d_ff_30 (.D(and_70_out), .clk(and_12_out), .Q(d_ff_30_q));  // open: Qn, preset, reset
  and and_71 (and_71_out, and_13_out, Mode, D1in);
  D_Flip_Flop #(.trigger("high")) d_ff_31 (.D(and_71_out), .clk(and_14_out), .Q(d_ff_31_q));  // open: Qn, preset, reset
  and and_72 (and_72_out, and_15_out, Mode, D1in);
  D_Flip_Flop #(.trigger("high")) d_ff_32 (.D(and_72_out), .clk(and_16_out), .Q(RAM0_0));  // open: Qn, preset, reset
  or or_4 (D1out, and_73_out, and_74_out, and_75_out, and_76_out, and_77_out, and_78_out, and_79_out, and_80_out);
  and and_73 (and_73_out, d_ff_25_q, and_1_out, not_13_out);
  and and_74 (and_74_out, d_ff_26_q, and_3_out, not_13_out);
  and and_75 (and_75_out, d_ff_27_q, and_5_out, not_13_out);
  and and_76 (and_76_out, d_ff_28_q, and_7_out, not_13_out);
  and and_77 (and_77_out, d_ff_29_q, and_9_out, not_13_out);
  and and_78 (and_78_out, d_ff_30_q, and_11_out, not_13_out);
  and and_79 (and_79_out, d_ff_31_q, and_13_out, not_13_out);
  and and_80 (and_80_out, RAM0_0, and_15_out, not_13_out);

  // Notes on the sheet:
  //   3-bit address input pins
  //   Mode input pin
  //   4-bit data input pins
  //   4-bit data output pins
endmodule

module ALU (
  input  L3,
  input  L2,
  input  L1,
  input  L0,
  input  R3,
  input  R2,
  input  R1,
  input  R0,
  input  CLCK,
  input  SUB,
  output Zero,
  output Negative,
  output Overflow,
  output AOUT3,
  output AOUT2,
  output AOUT1,
  output AOUT0
);

  wire and_1_out, and_2_out, and_3_out, and_4_out, and_5_out, and_6_out, and_7_out, and_8_out, and_9_out,
       and_10_out, and_11_out, and_12_out, and_13_out, and_14_out, and_15_out, and_16_out, and_17_out,
       and_18_out, and_19_out, and_20_out, and_21_out, and_22_out, and_24_out, and_25_out, and_26_out,
       and_27_out, fulladder_1_c, fulladder_2_c, fulladder_3_c, Neg_out, not_1_out, not_2_out, not_3_out,
       not_4_out, not_5_out, not_6_out, not_7_out, not_8_out, not_9_out, not_10_out, not_11_out, not_12_out,
       not_13_out, not_14_out, not_15_out, or_1_out, or_2_out, or_3_out, or_4_out, or_5_out, Pos_out,
       xor_2_out, xor_3_out, xor_4_out, xor_5_out;

  not not_1 (not_1_out, SUB);
  and and_1 (and_1_out, L3, CLCK);
  and and_2 (and_2_out, L2, CLCK);
  and and_3 (and_3_out, L1, CLCK);
  FullAdder fulladder_1 (.A(or_1_out), .B(and_1_out), .Carry(fulladder_2_c), .C(fulladder_1_c), .Sum(AOUT3));
  and and_4 (and_4_out, L0, CLCK);
  FullAdder fulladder_2 (.A(or_2_out), .B(and_2_out), .Carry(fulladder_3_c), .C(fulladder_2_c), .Sum(AOUT2));
  or or_1 (or_1_out, xor_2_out, and_6_out);
  FullAdder fulladder_3 (.A(or_3_out), .B(and_3_out), .Carry(and_5_out), .C(fulladder_3_c), .Sum(AOUT1));
  or or_2 (or_2_out, xor_3_out, and_8_out);
  or or_3 (or_3_out, xor_4_out, and_9_out);
  and and_5 (and_5_out, and_4_out, or_4_out);
  xor xor_1 (AOUT0, and_4_out, or_4_out);
  and and_6 (and_6_out, and_12_out, not_1_out);
  and and_7 (and_7_out, not_6_out, and_10_out);
  or or_4 (or_4_out, xor_5_out, and_14_out);
  not not_2 (not_2_out, AOUT0);
  not not_3 (not_3_out, AOUT1);
  not not_4 (not_4_out, AOUT2);
  not not_5 (not_5_out, AOUT3);
  and and_8 (and_8_out, and_13_out, not_1_out);
  and and_9 (and_9_out, and_17_out, not_1_out);
  xor xor_2 (xor_2_out, not_6_out, and_10_out);
  and and_10 (and_10_out, not_10_out, and_16_out);
  and and_11 (and_11_out, not_2_out, not_3_out, not_4_out, not_5_out);
  and and_12 (and_12_out, R3, CLCK);
  and and_13 (and_13_out, R2, CLCK);
  and and_14 (and_14_out, and_18_out, not_1_out);
  and and_15 (and_15_out, and_12_out, SUB);
  not not_6 (not_6_out, and_15_out);
  xor xor_3 (xor_3_out, not_10_out, and_16_out);
  and and_16 (and_16_out, not_11_out, and_22_out);
  not not_7 (not_7_out, or_1_out);
  not not_8 (not_8_out, and_1_out);
  not not_9 (not_9_out, or_1_out);
  and and_17 (and_17_out, R1, CLCK);
  and and_18 (and_18_out, R0, CLCK);
  and and_19 (and_19_out, and_13_out, SUB);
  and and_20 (and_20_out, and_17_out, SUB);
  and and_21 (and_21_out, and_18_out, SUB);
  not not_10 (not_10_out, and_19_out);
  not not_11 (not_11_out, and_20_out);
  not not_12 (not_12_out, and_21_out);
  xor xor_4 (xor_4_out, not_11_out, and_22_out);
  and and_22 (and_22_out, not_12_out, 1'b1);
  and Neg (Neg_out, or_1_out, and_1_out);
  and Pos (Pos_out, not_7_out, not_8_out);
  and and_23 (Zero, and_11_out, CLCK);
  xor xor_5 (xor_5_out, not_12_out, 1'b1);
  and and_24 (and_24_out, AOUT3, Neg_out);
  and and_25 (and_25_out, Pos_out, AOUT3);
  and and_26 (and_26_out, not_13_out, not_9_out, fulladder_1_c);
  not not_13 (not_13_out, SUB);
  not not_14 (not_14_out, fulladder_1_c);
  and and_27 (and_27_out, and_24_out, not_14_out);
  or or_5 (or_5_out, and_26_out, and_25_out, and_27_out);
  not not_15 (not_15_out, Zero);
  and notZero (Overflow, or_5_out, not_15_out);

  assign Negative = AOUT3;

  // Other names for the same wires on the sheet: CMD = SUB

  // Notes on the sheet:
  //   Add/Sub command
  //   0 add, 1 sub
  //   B Input
  //   L input
  //   A-out output
  //   A Input
  //   Adder
  //   R Input
  //   2's Complement
  //   Status output
  //   -8 + -8 is underflow (not supported)
endmodule

module FullAdder (
  input  A,
  input  B,
  input  Carry,
  output C,
  output Sum
);

  wire and_1_out, and_2_out, xor_1_out;

  and and_1 (and_1_out, A, B);
  xor xor_1 (xor_1_out, A, B);
  and and_2 (and_2_out, xor_1_out, Carry);
  or or_1 (C, and_1_out, and_2_out);
  xor xor_2 (Sum, xor_1_out, Carry);
endmodule

module MBR (
  input  CLCK,
  input  WRITE_MBR,
  input  D0,
  input  D1,
  input  D2,
  input  D3,
  output D0OUT,
  output D1OUT,
  output D2OUT,
  output D3OUT
);

  wire and_1_out, d_ff_1_q, d_ff_2_q, d_ff_3_q, d_ff_4_q, not_1_out;

  and and_1 (and_1_out, WRITE_MBR, CLCK);
  D_Flip_Flop #(.trigger("falling")) d_ff_1 (.D(D0), .clk(and_1_out), .Q(d_ff_1_q));  // open: Qn, preset, reset
  D_Flip_Flop #(.trigger("falling")) d_ff_2 (.D(D1), .clk(and_1_out), .Q(d_ff_2_q));  // open: Qn, preset, reset
  D_Flip_Flop #(.trigger("falling")) d_ff_3 (.D(D2), .clk(and_1_out), .Q(d_ff_3_q));  // open: Qn, preset, reset
  D_Flip_Flop #(.trigger("falling")) d_ff_4 (.D(D3), .clk(and_1_out), .Q(d_ff_4_q));  // open: Qn, preset, reset
  not not_1 (not_1_out, WRITE_MBR);
  and and_2 (D0OUT, d_ff_1_q, not_1_out);
  and and_3 (D1OUT, d_ff_2_q, not_1_out);
  and and_4 (D2OUT, d_ff_3_q, not_1_out);
  and and_5 (D3OUT, d_ff_4_q, not_1_out);
endmodule

module IR (
  input  CLCK,
  input  WRITE_IR,
  input  D0,
  input  D1,
  input  D2,
  input  D3,
  output D0OUT,
  output D1OUT,
  output D2OUT,
  output D3OUT
);

  wire and_1_out, d_ff_1_q, d_ff_2_q, d_ff_3_q, d_ff_4_q, not_1_out;

  and and_1 (and_1_out, WRITE_IR, CLCK);
  D_Flip_Flop #(.trigger("falling")) d_ff_1 (.D(D0), .clk(and_1_out), .Q(d_ff_1_q));  // open: Qn, preset, reset
  D_Flip_Flop #(.trigger("falling")) d_ff_2 (.D(D1), .clk(and_1_out), .Q(d_ff_2_q));  // open: Qn, preset, reset
  D_Flip_Flop #(.trigger("falling")) d_ff_3 (.D(D2), .clk(and_1_out), .Q(d_ff_3_q));  // open: Qn, preset, reset
  D_Flip_Flop #(.trigger("falling")) d_ff_4 (.D(D3), .clk(and_1_out), .Q(d_ff_4_q));  // open: Qn, preset, reset
  not not_1 (not_1_out, WRITE_IR);
  and and_2 (D0OUT, d_ff_1_q, not_1_out);
  and and_3 (D1OUT, d_ff_2_q, not_1_out);
  and and_4 (D2OUT, d_ff_3_q, not_1_out);
  and and_5 (D3OUT, d_ff_4_q, not_1_out);
endmodule

module MAR (
  input  CLCK,
  input  WRITE_MAR,
  input  A2,
  input  A1,
  input  A0,
  output A0OUT,
  output A1OUT,
  output A2OUT
);

  wire and_1_out, d_ff_1_q, d_ff_2_q, d_ff_3_q, not_1_out;

  and and_1 (and_1_out, WRITE_MAR, CLCK);
  D_Flip_Flop #(.trigger("falling")) d_ff_1 (.D(A0), .clk(and_1_out), .Q(d_ff_1_q));  // open: Qn, preset, reset
  D_Flip_Flop #(.trigger("falling")) d_ff_2 (.D(A1), .clk(and_1_out), .Q(d_ff_2_q));  // open: Qn, preset, reset
  D_Flip_Flop #(.trigger("falling")) d_ff_3 (.D(A2), .clk(and_1_out), .Q(d_ff_3_q));  // open: Qn, preset, reset
  not not_1 (not_1_out, WRITE_MAR);
  and and_2 (A0OUT, d_ff_1_q, not_1_out);
  and and_3 (A1OUT, d_ff_2_q, not_1_out);
  and and_4 (A2OUT, d_ff_3_q, not_1_out);
endmodule

module PC (
  input  RESET,
  input  CLCK,
  input  ADD_TO_PC,
  input  READ_PC,
  output A2,
  output A1,
  output A0
);

  wire and_1_out, d_ff_1_q, d_ff_2_q, d_ff_3_q, incr_1_a0out, incr_1_a1out, incr_1_a2out;

  and and_1 (and_1_out, CLCK, ADD_TO_PC);
  D_Flip_Flop d_ff_1 (.D(incr_1_a0out), .clk(and_1_out), .Q(d_ff_1_q), .reset(RESET));  // open: Qn, preset
  D_Flip_Flop d_ff_2 (.D(incr_1_a1out), .clk(and_1_out), .Q(d_ff_2_q), .reset(RESET));  // open: Qn, preset
  D_Flip_Flop d_ff_3 (.D(incr_1_a2out), .clk(and_1_out), .Q(d_ff_3_q), .preset(RESET));  // open: Qn, reset
  and and_2 (A0, d_ff_3_q, READ_PC);
  and and_3 (A1, d_ff_2_q, READ_PC);
  and and_4 (A2, d_ff_1_q, READ_PC);
  INCR incr_1 (
    .A2(d_ff_3_q), .A1(d_ff_2_q), .A0(d_ff_1_q), .A2OUT(incr_1_a2out), .A1OUT(incr_1_a1out),
    .A0OUT(incr_1_a0out));
endmodule

module INCR (
  input  A2,
  input  A1,
  input  A0,
  output A2OUT,
  output A1OUT,
  output A0OUT
);

  wire and_1_out, and_2_out;

  xor xor_1 (A2OUT, 1'b1, A2);
  and and_1 (and_1_out, 1'b1, A2);
  xor xor_2 (A1OUT, and_1_out, A1);
  and and_2 (and_2_out, and_1_out, A1);
  xor xor_3 (A0OUT, and_2_out, A0);
endmodule

module R0 (
  input  D3,
  input  D2,
  input  D1,
  input  D0,
  input  WRITE_R0,
  input  CLCK,
  input  ENABLE,
  output D3OUT,
  output D2OUT,
  output D1OUT,
  output D0OUT
);

  wire and_1_out, d_ff_1_q, d_ff_2_q, d_ff_3_q, d_ff_4_q;

  and and_1 (and_1_out, WRITE_R0, CLCK);
  D_Flip_Flop #(.trigger("falling")) d_ff_1 (.D(D3), .clk(and_1_out), .Q(d_ff_1_q));  // open: Qn, preset, reset
  D_Flip_Flop #(.trigger("falling")) d_ff_2 (.D(D2), .clk(and_1_out), .Q(d_ff_2_q));  // open: Qn, preset, reset
  D_Flip_Flop #(.trigger("falling")) d_ff_3 (.D(D1), .clk(and_1_out), .Q(d_ff_3_q));  // open: Qn, preset, reset
  D_Flip_Flop #(.trigger("falling")) d_ff_4 (.D(D0), .clk(and_1_out), .Q(d_ff_4_q));  // open: Qn, preset, reset
  and and_2 (D3OUT, d_ff_1_q, ENABLE);
  and and_3 (D2OUT, d_ff_2_q, ENABLE);
  and and_4 (D1OUT, d_ff_3_q, ENABLE);
  and and_5 (D0OUT, d_ff_4_q, ENABLE);
endmodule

module R1 (
  input  D3,
  input  D2,
  input  D1,
  input  D0,
  input  WRITE_R1,
  input  CLCK,
  input  ENABLE,
  output D3OUT,
  output D2OUT,
  output D1OUT,
  output D0OUT
);

  wire and_1_out, d_ff_1_q, d_ff_2_q, d_ff_3_q, d_ff_4_q;

  and and_1 (and_1_out, WRITE_R1, CLCK);
  D_Flip_Flop #(.trigger("falling")) d_ff_1 (.D(D3), .clk(and_1_out), .Q(d_ff_1_q));  // open: Qn, preset, reset
  D_Flip_Flop #(.trigger("falling")) d_ff_2 (.D(D2), .clk(and_1_out), .Q(d_ff_2_q));  // open: Qn, preset, reset
  D_Flip_Flop #(.trigger("falling")) d_ff_3 (.D(D1), .clk(and_1_out), .Q(d_ff_3_q));  // open: Qn, preset, reset
  D_Flip_Flop #(.trigger("falling")) d_ff_4 (.D(D0), .clk(and_1_out), .Q(d_ff_4_q));  // open: Qn, preset, reset
  and and_2 (D3OUT, d_ff_1_q, ENABLE);
  and and_3 (D2OUT, d_ff_2_q, ENABLE);
  and and_4 (D1OUT, d_ff_3_q, ENABLE);
  and and_5 (D0OUT, d_ff_4_q, ENABLE);
endmodule

module ControlUnit (
  input  RESET,
  input  CLCK,
  input  IN1,
  input  IN2,
  input  IN3,
  input  IN4,
  output INCR_PC,
  output WRITE_MBR,
  output WRITE_IR,
  output A0,
  output WRITE_R0,
  output WRITE_R1,
  output ENABLE_R0,
  output ENABLE_R1,
  output ENABLE_RAM,
  output WRITE_RAM,
  output WRITE_MAR,
  output MODE_ALU,
  output ENABLE_LEFT,
  output ENABLE_RIGHT,
  output READ_PC,
  output READ_LEFT,
  output READ_RIGHT,
  output WRITE_AR,
  output READ_AR,
  output HALT
);

  wire choose_1_add, choose_1_load, choose_1_save, choose_1_sub_halt;

  Choose choose_1 (
    .CLCK(CLCK), .IN4(IN4), .IN3(IN3), .LOAD(choose_1_load), .SAVE(choose_1_save), .ADD(choose_1_add),
    .SUB_HALT(choose_1_sub_halt));
  IC ic_1 (
    .RESET(RESET), .CLCK(CLCK), .IN2(IN2), .IN1(IN1), .LOAD(choose_1_load), .SAVE(choose_1_save),
    .ADD(choose_1_add), .SUB_HALT(choose_1_sub_halt), .INCR_PC(INCR_PC), .WRITE_MBR(WRITE_MBR),
    .WRITE_IR(WRITE_IR), .A0(A0), .WRITE_R0(WRITE_R0), .WRITE_R1(WRITE_R1), .ENABLE_R0(ENABLE_R0),
    .ENABLE_R1(ENABLE_R1), .ENABLE_RAM(ENABLE_RAM), .WRITE_RAM(WRITE_RAM), .WRITE_MAR(WRITE_MAR),
    .MODE_ALU(MODE_ALU), .ENABLE_LEFT(ENABLE_LEFT), .ENABLE_RIGHT(ENABLE_RIGHT), .READ_PC(READ_PC),
    .READ_LEFT(READ_LEFT), .READ_RIGHT(READ_RIGHT), .WRITE_AR(WRITE_AR), .READ_AR(READ_AR), .HALT(HALT));
endmodule

module Choose (
  input  CLCK,
  input  IN4,
  input  IN3,
  output LOAD,
  output SAVE,
  output ADD,
  output SUB_HALT
);

  wire and_1_out, and_2_out, and_3_out;

  and and_1 (and_1_out, ~IN4, ~IN3);  // AND_Gate
  and and_2 (and_2_out, ~IN4, IN3);  // AND_Gate
  and and_3 (and_3_out, IN4, ~IN3);  // AND_Gate
  and and_4 (SUB_HALT, IN4, IN3);
  and and_5 (LOAD, and_1_out, CLCK);
  and and_6 (SAVE, and_2_out, CLCK);
  and and_7 (ADD, and_3_out, CLCK);
endmodule

module IC (
  input  RESET,
  input  CLCK,
  input  IN2,
  input  IN1,
  input  LOAD,
  input  SAVE,
  input  ADD,
  input  SUB_HALT,
  output INCR_PC,
  output WRITE_MBR,
  output WRITE_IR,
  output A0,
  output WRITE_R0,
  output WRITE_R1,
  output ENABLE_R0,
  output ENABLE_R1,
  output ENABLE_RAM,
  output WRITE_RAM,
  output WRITE_MAR,
  output MODE_ALU,
  output ENABLE_LEFT,
  output ENABLE_RIGHT,
  output READ_PC,
  output READ_LEFT,
  output READ_RIGHT,
  output WRITE_AR,
  output READ_AR,
  output HALT
);

  wire and_2_out, and_3_out, and_4_out, and_5_out, and_6_out, and_7_out, and_8_out, and_9_out, and_10_out,
       and_11_out, and_12_out, and_13_out, and_14_out, and_15_out, and_16_out, and_17_out, and_18_out,
       count_step_1_s1, count_step_1_s2, count_step_1_s3, fetch_cycle_1_enable_ram, fetch_cycle_1_read_pc,
       fetch_cycle_1_write_mar, or_1_out, or_2_out, STEP4, STEP5, STEP6;

  and and_1 (HALT, SUB_HALT, IN2, IN1);
  buf and_2 (and_2_out, CLCK);  // AND_Gate AND_Gate
  COUNT_STEP count_step_1 (
    .CLCK(and_2_out), .Reset(RESET), .S1(count_step_1_s1), .S2(count_step_1_s2), .S3(count_step_1_s3),
    .S4(STEP4), .S5(STEP5), .S6(STEP6));
  or or_1 (or_1_out, count_step_1_s1, count_step_1_s2, count_step_1_s3);
  and and_3 (and_3_out, ~HALT, or_1_out);  // AND_Gate
  or or_2 (or_2_out, ADD, SUB_HALT);
  and and_4 (and_4_out, STEP4, LOAD);
  and and_5 (and_5_out, STEP5, LOAD);
  and and_6 (and_6_out, STEP6, LOAD);
  and and_7 (and_7_out, STEP6, SAVE);
  and and_8 (and_8_out, STEP4, SAVE);
  and and_9 (and_9_out, STEP5, SAVE);
  and and_10 (and_10_out, or_2_out, STEP4);
  and and_11 (and_11_out, or_2_out, STEP5);
  and and_12 (and_12_out, or_2_out, STEP6);
  FETCH_CYCLE fetch_cycle_1 (
    .CLCK(and_2_out), .RESET(RESET), .ENABLE_FETCH(and_3_out), .WRITE_MAR(fetch_cycle_1_write_mar),
    .INCR_PC(INCR_PC), .READ_PC(fetch_cycle_1_read_pc), .ENABLE_RAM(fetch_cycle_1_enable_ram),
    .WRITE_MBR(WRITE_MBR), .WRITE_IR(WRITE_IR));
  or or_3 (WRITE_AR, and_4_out, and_8_out);
  and and_13 (and_13_out, and_6_out, ~IN2);  // AND_Gate
  and and_14 (and_14_out, and_6_out, IN2);
  and and_15 (and_15_out, and_7_out, ~IN2);  // AND_Gate
  and and_16 (and_16_out, and_7_out, IN2);
  and and_17 (and_17_out, and_11_out, ~IN2);  // AND_Gate
  and and_18 (and_18_out, and_11_out, IN2);
  and and_19 (MODE_ALU, SUB_HALT, ~HALT);  // AND_Gate
  or or_4 (WRITE_R0, and_13_out, and_12_out);
  buf or_5 (WRITE_R1, and_14_out);  // OR_Gate
  or or_6 (ENABLE_R0, and_15_out, and_17_out, and_10_out);
  or or_7 (ENABLE_R1, and_16_out, and_18_out);
  buf or_8 (ENABLE_RAM, fetch_cycle_1_enable_ram);  // OR_Gate
  or or_9 (WRITE_RAM, and_15_out, and_16_out);
  or or_10 (WRITE_MAR, fetch_cycle_1_write_mar, and_9_out, and_5_out);
  buf or_11 (ENABLE_LEFT, and_10_out);  // OR_Gate
  or or_12 (ENABLE_RIGHT, and_17_out, and_18_out);
  buf or_13 (READ_PC, fetch_cycle_1_read_pc);  // OR_Gate
  buf or_14 (READ_LEFT, and_12_out);  // OR_Gate
  buf or_15 (READ_RIGHT, and_12_out);  // OR_Gate
  or or_16 (READ_AR, and_5_out, and_9_out);
  // AND_Gate and_20 has open pins: in0=WRITE_R0, in1=HALT, out=open
  // AND_Gate and_21 has open pins: in0=WRITE_R1, in1=HALT, out=open

  assign A0 = IN1;

  // Notes on the sheet:
  //   HALT
endmodule

module COUNT_STEP (
  input  CLCK,
  input  Reset,
  output S1,
  output S2,
  output S3,
  output S4,
  output S5,
  output S6
);

  wire and_1_out, d_ff_1_q, d_ff_2_q, d_ff_3_q, incr_1_a0out, incr_1_a1out, incr_1_a2out, not_1_out, or_1_out;

  not not_1 (not_1_out, CLCK);
  or or_1 (or_1_out, Reset, and_1_out);
  D_Flip_Flop d_ff_1 (.D(incr_1_a0out), .clk(not_1_out), .Q(d_ff_1_q), .reset(or_1_out));  // open: Qn, preset
  D_Flip_Flop d_ff_2 (.D(incr_1_a1out), .clk(not_1_out), .Q(d_ff_2_q), .reset(or_1_out));  // open: Qn, preset
  and and_1 (and_1_out, d_ff_1_q, d_ff_2_q);
  D_Flip_Flop d_ff_3 (.D(incr_1_a2out), .clk(not_1_out), .Q(d_ff_3_q), .reset(or_1_out));  // open: Qn, preset
  and Step1 (S1, ~d_ff_1_q, ~d_ff_2_q, ~d_ff_3_q);  // AND_Gate
  and Step2 (S2, ~d_ff_1_q, ~d_ff_2_q, d_ff_3_q);  // AND_Gate
  and Step3 (S3, ~d_ff_1_q, d_ff_2_q, ~d_ff_3_q);  // AND_Gate
  and Step4 (S4, ~d_ff_1_q, d_ff_2_q, d_ff_3_q);  // AND_Gate
  and Step5 (S5, d_ff_1_q, ~d_ff_2_q, ~d_ff_3_q);  // AND_Gate
  and Step6 (S6, d_ff_1_q, ~d_ff_2_q, d_ff_3_q);  // AND_Gate
  INCR incr_1 (
    .A2(d_ff_3_q), .A1(d_ff_2_q), .A0(d_ff_1_q), .A2OUT(incr_1_a2out), .A1OUT(incr_1_a1out),
    .A0OUT(incr_1_a0out));
endmodule

module FETCH_CYCLE (
  input  CLCK,
  input  RESET,
  input  ENABLE_FETCH,
  output WRITE_MAR,
  output INCR_PC,
  output READ_PC,
  output ENABLE_RAM,
  output WRITE_MBR,
  output WRITE_IR
);

  wire count_step_1_s1, count_step_1_s2, count_step_1_s3;

  COUNT_STEP count_step_1 (
    .CLCK(CLCK), .Reset(RESET), .S1(count_step_1_s1), .S2(count_step_1_s2), .S3(count_step_1_s3));  // open: S4, S5, S6
  and and_1 (INCR_PC, count_step_1_s1, ENABLE_FETCH);
  and and_2 (ENABLE_RAM, count_step_1_s2, ENABLE_FETCH);
  and and_3 (WRITE_IR, count_step_1_s3, ENABLE_FETCH);

  assign READ_PC = INCR_PC;
  assign WRITE_MAR = INCR_PC;
  assign WRITE_MBR = ENABLE_RAM;
endmodule

module LEFT_REG (
  input  ENABLE_LEFT,
  input  CLCK,
  input  READ_LEFT,
  input  D3,
  input  D2,
  input  D1,
  input  D0,
  output D3_OUT,
  output D2_OUT,
  output D1_OUT,
  output D0_OUT
);

  wire and_1_out, d_ff_1_q, d_ff_2_q, d_ff_3_q, d_ff_4_q;

  and and_1 (and_1_out, ENABLE_LEFT, CLCK);
  D_Flip_Flop #(.trigger("falling")) d_ff_1 (.D(D3), .clk(and_1_out), .Q(d_ff_1_q));  // open: Qn, preset, reset
  D_Flip_Flop #(.trigger("falling")) d_ff_2 (.D(D2), .clk(and_1_out), .Q(d_ff_2_q));  // open: Qn, preset, reset
  D_Flip_Flop #(.trigger("falling")) d_ff_3 (.D(D1), .clk(and_1_out), .Q(d_ff_3_q));  // open: Qn, preset, reset
  D_Flip_Flop #(.trigger("falling")) d_ff_4 (.D(D0), .clk(and_1_out), .Q(d_ff_4_q));  // open: Qn, preset, reset
  and and_2 (D3_OUT, d_ff_1_q, READ_LEFT);
  and and_3 (D2_OUT, d_ff_2_q, READ_LEFT);
  and and_4 (D1_OUT, d_ff_3_q, READ_LEFT);
  and and_5 (D0_OUT, d_ff_4_q, READ_LEFT);
endmodule

module RIGHT_REG (
  input  ENABLE_RIGHT,
  input  CLCK,
  input  READ_RIGHT,
  input  D3,
  input  D2,
  input  D1,
  input  D0,
  output D3_OUT,
  output D2_OUT,
  output D1_OUT,
  output D0_OUT
);

  wire and_1_out, d_ff_1_q, d_ff_2_q, d_ff_3_q, d_ff_4_q;

  and and_1 (and_1_out, ENABLE_RIGHT, CLCK);
  D_Flip_Flop #(.trigger("falling")) d_ff_1 (.D(D3), .clk(and_1_out), .Q(d_ff_1_q));  // open: Qn, preset, reset
  D_Flip_Flop #(.trigger("falling")) d_ff_2 (.D(D2), .clk(and_1_out), .Q(d_ff_2_q));  // open: Qn, preset, reset
  D_Flip_Flop #(.trigger("falling")) d_ff_3 (.D(D1), .clk(and_1_out), .Q(d_ff_3_q));  // open: Qn, preset, reset
  D_Flip_Flop #(.trigger("falling")) d_ff_4 (.D(D0), .clk(and_1_out), .Q(d_ff_4_q));  // open: Qn, preset, reset
  and and_2 (D3_OUT, d_ff_1_q, READ_RIGHT);
  and and_3 (D2_OUT, d_ff_2_q, READ_RIGHT);
  and and_4 (D1_OUT, d_ff_3_q, READ_RIGHT);
  and and_5 (D0_OUT, d_ff_4_q, READ_RIGHT);
endmodule

module ADDRESS_REG (
  input  READ_ADDRREG,
  input  CLCK,
  input  WRITE_ADDREG,
  input  A0,
  input  A1,
  input  A2,
  output A2OUT,
  output A1OUT,
  output A0OUT
);

  wire and_1_out, d_ff_1_q, d_ff_2_q, d_ff_3_q, undriven;

  and and_1 (and_1_out, CLCK, WRITE_ADDREG);
  D_Flip_Flop #(.trigger("falling")) d_ff_1 (.D(A0), .clk(and_1_out), .Q(d_ff_1_q));  // open: Qn, preset, reset
  D_Flip_Flop #(.trigger("falling")) d_ff_2 (
    .D(A1), .clk(and_1_out), .Q(d_ff_2_q), .reset(undriven));  // open: Qn, preset
  D_Flip_Flop #(.trigger("falling")) d_ff_3 (.D(A2), .clk(and_1_out), .Q(d_ff_3_q));  // open: Qn, preset, reset
  and and_2 (A0OUT, d_ff_1_q, READ_ADDRREG);
  and and_3 (A1OUT, d_ff_2_q, READ_ADDRREG);
  and and_4 (A2OUT, d_ff_3_q, READ_ADDRREG);
endmodule

module D_REGISTER (
  input  D3,
  input  D2,
  input  D1,
  input  D0,
  input  CLCK,
  output D3OUT,
  output D2OUT,
  output D1OUT,
  output D0OUT
);

  D_Flip_Flop #(.trigger("falling")) d_ff_1 (.D(D3), .clk(CLCK), .Q(D3OUT));  // open: Qn, preset, reset
  D_Flip_Flop #(.trigger("falling")) d_ff_2 (.D(D2), .clk(CLCK), .Q(D2OUT));  // open: Qn, preset, reset
  D_Flip_Flop #(.trigger("falling")) d_ff_3 (.D(D1), .clk(CLCK), .Q(D1OUT));  // open: Qn, preset, reset
  D_Flip_Flop #(.trigger("falling")) d_ff_4 (.D(D0), .clk(CLCK), .Q(D0OUT));  // open: Qn, preset, reset
endmodule

module BINARY_TO_DECIMAL (
  input  D3,
  input  D2,
  input  D1,
  input  D0,
  output A0,
  output A1,
  output B0,
  output B1,
  output B2,
  output B3,
  output B4,
  output B5,
  output B6,
  output B7,
  output B8,
  output B9
);

  wire eight_out, eleven_out, fifteen_out, five_out, four_out, fourteen_out, nine_out, one_out, seven_out,
       six_out, ten_out, thirteen_out, three_out, twelve_out, two_out, zero_out;

  and zero (zero_out, ~D3, ~D2, ~D1, ~D0);  // AND_Gate
  and one (one_out, ~D3, ~D2, ~D1, D0);  // AND_Gate
  and two (two_out, ~D3, ~D2, D1, ~D0);  // AND_Gate
  and three (three_out, ~D3, ~D2, D1, D0);  // AND_Gate
  and four (four_out, ~D3, D2, ~D1, ~D0);  // AND_Gate
  and five (five_out, ~D3, D2, ~D1, D0);  // AND_Gate
  and six (six_out, ~D3, D2, D1, ~D0);  // AND_Gate
  and seven (seven_out, ~D3, D2, D1, D0);  // AND_Gate
  and eight (eight_out, D3, ~D2, ~D1, ~D0);  // AND_Gate
  and nine (nine_out, D3, ~D2, ~D1, D0);  // AND_Gate
  and ten (ten_out, D3, ~D2, D1, ~D0);  // AND_Gate
  and eleven (eleven_out, D3, ~D2, D1, D0);  // AND_Gate
  and twelve (twelve_out, D3, D2, ~D1, ~D0);  // AND_Gate
  and thirteen (thirteen_out, D3, D2, ~D1, D0);  // AND_Gate
  and fourteen (fourteen_out, D3, D2, D1, ~D0);  // AND_Gate
  and fifteen (fifteen_out, D3, D2, D1, D0);
  or or_1 (A0, zero_out, one_out, two_out, three_out, four_out, five_out, six_out, seven_out, eight_out, nine_out);
  or or_2 (B0, zero_out, ten_out);
  or or_3 (B1, one_out, eleven_out);
  or or_4 (B2, two_out, twelve_out);
  or or_5 (B3, three_out, thirteen_out);
  or or_6 (B4, four_out, fourteen_out);
  or or_7 (B5, five_out, fifteen_out);
  buf or_8 (B6, six_out);  // OR_Gate
  buf or_9 (B7, seven_out);  // OR_Gate
  buf or_10 (B8, eight_out);  // OR_Gate
  buf or_11 (B9, nine_out);  // OR_Gate
  not not_1 (A1, A0);

  // Notes on the sheet:
  //   FIRST DIGIT
  //   SECOND DIGIT
endmodule

module NUMS (
  input  Z_ERO,
  input  O_NE,
  input  TWO,
  input  THREE,
  input  FOUR,
  input  FIVE,
  input  SIX,
  input  SEVEN,
  input  EIGHT,
  input  NINE,
  output FIRST,
  output SECOND,
  output THIRD,
  output FOURTH,
  output FIFTH,
  output SIXTH,
  output SEVENTH
);

  or or_1 (FIRST, EIGHT, THREE, TWO, FIVE, NINE, FOUR, SIX);
  or or_2 (SECOND, FIVE, SIX, EIGHT, FOUR, Z_ERO, O_NE, NINE);
  or or_3 (THIRD, Z_ERO, TWO, THREE, FIVE, SIX, SEVEN, EIGHT, NINE);
  or or_4 (FOURTH, Z_ERO, THREE, FOUR, SEVEN, EIGHT, NINE, NINE, TWO);
  or or_5 (FIFTH, THREE, FOUR, FIVE, SIX, SEVEN, EIGHT, NINE, Z_ERO);
  or or_6 (SIXTH, Z_ERO, TWO, THREE, FIVE, SIX, EIGHT);
  or or_7 (SEVENTH, Z_ERO, O_NE, TWO, SIX, EIGHT);
endmodule

module StatusReg (
  input  ZERO,
  input  NEGATIVE,
  input  OVERFLOW,
  input  CLCK
);

  wire d_ff_1_q, d_ff_2_q, d_ff_3_q;

  D_Flip_Flop #(.trigger("falling")) d_ff_1 (.D(ZERO), .clk(CLCK), .Q(d_ff_1_q));  // open: Qn, preset, reset
  D_Flip_Flop #(.trigger("falling")) d_ff_2 (.D(NEGATIVE), .clk(CLCK), .Q(d_ff_2_q));  // open: Qn, preset, reset
  D_Flip_Flop #(.trigger("falling")) d_ff_3 (.D(OVERFLOW), .clk(CLCK), .Q(d_ff_3_q));  // open: Qn, preset, reset
endmodule
